// Logisim project GT-2200.circ as structural Verilog: 4 circuits, main circuit my circuit
module my_circuit (
  output [3:0] regno,
  output [5:0] NextState
);

  wire bit_extender_1_out, CLK, CmpOut, comparator_1_eq, comparator_1_gt, DrALU, DrMEM, DrOFF, DrPC, DrREG,
       LdA, LdB, LdCmp, LdIR, LdMAR, LdPC, multiplexer_1_out, WrMEM, WrReg;
  wire [1:0] func, RegSel;
  wire [3:0] mode, OP, Ry, Rz;
  wire [19:4] IR_q;
  wire [23:0] bit_extender_2_out;
  wire [31:0] A_q, ALU_output, B_q, bit_extender_3_out, controlled_buffer_1_out, MAR_q, PC_q, ram_1_data,
       register_file_1_output;

  Register #(.width(32)) PC (.D(controlled_buffer_1_out), .en(LdPC), .Q(PC_q), .clk(CLK));  // open: clr
  assign controlled_buffer_1_out = DrPC ? PC_q : 32'bz;  // Controlled_Buffer controlled_buffer_1
  Register #(.width(32)) B (.D(controlled_buffer_1_out), .en(LdB), .Q(B_q), .clk(CLK));  // open: clr
  Comparator #(.width(32)) comparator_1 (
    .a(controlled_buffer_1_out), .b({32{1'b0}}), .gt(comparator_1_gt), .eq(comparator_1_eq));  // open: lt
  Bit_Extender #(.in_width(4), .out_width(1)) bit_extender_1 (.in(mode), .out(bit_extender_1_out));
  ALU ALU (.A(A_q), .B(B_q), .func(func), .\output (ALU_output));
  assign controlled_buffer_1_out = DrALU ? ALU_output : 32'bz;  // Controlled_Buffer controlled_buffer_2
  Multiplexer #(.disabled(0), .enable("false")) multiplexer_1 (
    .in0(comparator_1_eq), .in1(comparator_1_gt), .out(multiplexer_1_out), .sel(bit_extender_1_out));
  Register #(.width(32)) A (.D(controlled_buffer_1_out), .en(LdA), .Q(A_q), .clk(CLK));  // open: clr
  Register #(.width(1), .trigger("falling")) CmpReg (
    .D(multiplexer_1_out), .en(LdCmp), .Q(CmpOut), .clk(CLK));  // open: clr
  Register_File register_file_1 (
    .Input(controlled_buffer_1_out), .regno(regno), .WrReg(WrReg), .clock(CLK),
    .Output(register_file_1_output));
  assign controlled_buffer_1_out = DrREG ? register_file_1_output : 32'bz;  // Controlled_Buffer controlled_buffer_3
  Register #(.width(32)) MAR (.D(controlled_buffer_1_out), .en(LdMAR), .Q(MAR_q), .clk(CLK));  // open: clr
  RAM #(.addrWidth(24), .dataWidth(32), .bus("separate")) ram_1 (
    .addr(bit_extender_2_out), .din(controlled_buffer_1_out), .data(ram_1_data), .str(WrMEM), .clk(CLK));  // open: sel, ld, clr
  Bit_Extender #(.in_width(32), .out_width(24)) bit_extender_2 (.in(MAR_q), .out(bit_extender_2_out));
  assign controlled_buffer_1_out = DrMEM ? ram_1_data : 32'bz;  // Controlled_Buffer controlled_buffer_4
  Microcontrol_Unit microcontrol_unit_1 (
    .func(func), .RegSel(RegSel), .WrMEM(WrMEM), .WrREG(WrReg), .LdCmp(LdCmp), .LdB(LdB), .LdA(LdA),
    .LdMAR(LdMAR), .LdIR(LdIR), .LdPC(LdPC), .DrOFF(DrOFF), .DrPC(DrPC), .DrALU(DrALU), .DrMEM(DrMEM),
    .DrREG(DrREG), .CmpOut(CmpOut), .CLK(CLK), .nextstate(NextState), .OP(OP));
  assign bit_extender_3_out = {{12{IR_q[19]}}, {IR_q, Rz}};  // Bit_Extender bit_extender_3
  assign controlled_buffer_1_out = DrOFF ? bit_extender_3_out : 32'bz;  // Controlled_Buffer controlled_buffer_5
  Register #(.width(32)) IR (
    .D(controlled_buffer_1_out), .en(LdIR), .Q({OP, mode, Ry, IR_q, Rz}), .clk(CLK));  // open: clr
  Clock clock_1 (.out(CLK));
  Multiplexer #(.select(2), .width(4), .disabled(0), .enable("false")) multiplexer_2 (
    .in0(mode), .in1(Ry), .in2(Rz), .out(regno), .sel(RegSel));  // open: in3

  // Other names for the same wires on the sheet: Rx[3:0] = mode
endmodule

module ALU (
  input  [31:0] A,
  input  [31:0] B,
  input  [1:0] func,
  output [31:0] \output 
);

  wire [31:0] adder_1_out, adder_2_out, nand_1_out, subtractor_1_out;

  Adder #(.width(32)) adder_1 (.a(A), .b(B), .out(adder_1_out), .cin(1'b0));  // open: cout
  Subtractor #(.width(32)) subtractor_1 (.a(A), .b(B), .out(subtractor_1_out), .bin(1'b0));  // open: bout
  assign nand_1_out = ~(A & B);  // NAND_Gate nand_1, 32 bits wide
  Adder #(.width(32)) adder_2 (.a(A), .b(32'h1), .out(adder_2_out));  // open: cin, cout
  Multiplexer #(.select(2), .width(32), .disabled(0), .enable("false")) multiplexer_1 (
    .in0(adder_1_out), .in1(subtractor_1_out), .in2(nand_1_out), .in3(adder_2_out), .out(\output ), .sel(func));
endmodule

module Register_File (
  input  [3:0] regno,
  input  WrReg,
  input  clock,
  input  [31:0] Input,
  output [31:0] Output
);

  wire reg1, reg2, reg3, reg4, reg5, reg6, reg7, reg8, reg9, reg10, reg11, reg12, reg13, reg14, reg15;
  wire [31:0] demultiplexer_1_out1, demultiplexer_1_out2, demultiplexer_1_out3, demultiplexer_1_out4,
       demultiplexer_1_out5, demultiplexer_1_out6, demultiplexer_1_out7, demultiplexer_1_out8,
       demultiplexer_1_out9, demultiplexer_1_out10, demultiplexer_1_out11, demultiplexer_1_out12,
       demultiplexer_1_out13, demultiplexer_1_out14, demultiplexer_1_out15, Reg1_q, Reg2_q, Reg3_q, Reg4_q,
       Reg5_q, Reg6_q, Reg7_q, Reg8_q, Reg9_q, Reg10_q, Reg11_q, Reg12_q, Reg13_q, Reg14_q, Reg15_q;

  Demultiplexer #(.select(4), .width(32), .disabled(0), .enable("false")) demultiplexer_1 (
    .out1(demultiplexer_1_out1), .out2(demultiplexer_1_out2), .out3(demultiplexer_1_out3),
    .out4(demultiplexer_1_out4), .out5(demultiplexer_1_out5), .out6(demultiplexer_1_out6),
    .out7(demultiplexer_1_out7), .out8(demultiplexer_1_out8), .out9(demultiplexer_1_out9),
    .out10(demultiplexer_1_out10), .out11(demultiplexer_1_out11), .out12(demultiplexer_1_out12),
    .out13(demultiplexer_1_out13), .out14(demultiplexer_1_out14), .out15(demultiplexer_1_out15), .in(Input),
    .sel(regno));  // open: out0
  Register #(.width(32)) u_Reg1 (.D(demultiplexer_1_out1), .en(reg1), .Q(Reg1_q), .clk(clock));  // open: clr
  Register #(.width(32)) u_Reg2 (.D(demultiplexer_1_out2), .en(reg2), .Q(Reg2_q), .clk(clock));  // open: clr
  Register #(.width(32)) u_Reg3 (.D(demultiplexer_1_out3), .en(reg3), .Q(Reg3_q), .clk(clock));  // open: clr
  Register #(.width(32)) u_Reg4 (.D(demultiplexer_1_out4), .en(reg4), .Q(Reg4_q), .clk(clock));  // open: clr
  Register #(.width(32)) u_Reg5 (.D(demultiplexer_1_out5), .en(reg5), .Q(Reg5_q), .clk(clock));  // open: clr
  Register #(.width(32)) u_Reg6 (.D(demultiplexer_1_out6), .en(reg6), .Q(Reg6_q), .clk(clock));  // open: clr
  Register #(.width(32)) u_Reg7 (.D(demultiplexer_1_out7), .en(reg7), .Q(Reg7_q), .clk(clock));  // open: clr
  Register #(.width(32)) u_Reg8 (.D(demultiplexer_1_out8), .en(reg8), .Q(Reg8_q), .clk(clock));  // open: clr
  Register #(.width(32)) u_Reg9 (.D(demultiplexer_1_out9), .en(reg9), .Q(Reg9_q), .clk(clock));  // open: clr
  Register #(.width(32)) u_Reg10 (.D(demultiplexer_1_out10), .en(reg10), .Q(Reg10_q), .clk(clock));  // open: clr
  Register #(.width(32)) u_Reg11 (.D(demultiplexer_1_out11), .en(reg11), .Q(Reg11_q), .clk(clock));  // open: clr
  Register #(.width(32)) u_Reg12 (.D(demultiplexer_1_out12), .en(reg12), .Q(Reg12_q), .clk(clock));  // open: clr
  Register #(.width(32)) u_Reg13 (.D(demultiplexer_1_out13), .en(reg13), .Q(Reg13_q), .clk(clock));  // open: clr
  Register #(.width(32)) u_Reg14 (.D(demultiplexer_1_out14), .en(reg14), .Q(Reg14_q), .clk(clock));  // open: clr
  Register #(.width(32)) u_Reg15 (.D(demultiplexer_1_out15), .en(reg15), .Q(Reg15_q), .clk(clock));  // open: clr
  Multiplexer #(.select(4), .width(32), .disabled(0), .enable("false")) multiplexer_1 (
    .in0({32{1'b0}}), .in1(Reg1_q), .in2(Reg2_q), .in3(Reg3_q), .in4(Reg4_q), .in5(Reg5_q), .in6(Reg6_q),
    .in7(Reg7_q), .in8(Reg8_q), .in9(Reg9_q), .in10(Reg10_q), .in11(Reg11_q), .in12(Reg12_q), .in13(Reg13_q),
    .in14(Reg14_q), .in15(Reg15_q), .out(Output), .sel(regno));
  Demultiplexer #(.select(4), .disabled(0), .enable("false")) demultiplexer_2 (
    .out1(reg1), .out2(reg2), .out3(reg3), .out4(reg4), .out5(reg5), .out6(reg6), .out7(reg7), .out8(reg8),
    .out9(reg9), .out10(reg10), .out11(reg11), .out12(reg12), .out13(reg13), .out14(reg14), .out15(reg15),
    .in(WrReg), .sel(regno));  // open: out0

  // Other names for the same wires on the sheet: CLK = clock
endmodule

module Microcontrol_Unit (
  input  [3:0] OP,
  input  CmpOut,
  input  CLK,
  output [1:0] func,
  output [1:0] RegSel,
  output WrMEM,
  output WrREG,
  output LdCmp,
  output LdB,
  output LdA,
  output LdMAR,
  output LdIR,
  output LdPC,
  output DrOFF,
  output DrPC,
  output DrALU,
  output DrMEM,
  output DrREG,
  output [5:0] nextstate
);

  wire [1:0] bit_extender_1_out, ChkCmp_OPTest;
  wire [5:0] multiplexer_1_out, rom_2_data, rom_3_data, State_Register_q;

  Register #(.width(6)) State_Register (.D(multiplexer_1_out), .Q(State_Register_q), .clk(CLK));  // open: en, clr
  ROM #(.addrWidth(6), .dataWidth(25)) rom_1 (
    .addr(State_Register_q),
    .data({ChkCmp_OPTest, func, RegSel, WrMEM, WrREG, LdCmp, LdB, LdA, LdMAR, LdIR, LdPC, DrOFF, DrPC, DrALU, DrMEM, DrREG, nextstate}));  // open: sel
  Multiplexer #(.select(2), .width(6), .disabled(0), .enable("false")) multiplexer_1 (
    .in0(nextstate), .in1(rom_2_data), .in2(rom_3_data), .out(multiplexer_1_out), .sel(ChkCmp_OPTest));  // open: in3
  assign bit_extender_1_out = {{1{1'b0}}, CmpOut};  // Bit_Extender bit_extender_1
  ROM #(.addrWidth(4), .dataWidth(6)) rom_2 (.addr(OP), .data(rom_2_data));  // open: sel
  ROM #(.addrWidth(2), .dataWidth(6)) rom_3 (.addr(bit_extender_1_out), .data(rom_3_data));  // open: sel

  // Notes on the sheet:
  //   contents of rom_1 (hex, n*v repeats v):
  //   6201 1082 e00900 84044 108045 20100 84047 108048 420100 8404a 840b 20100 420d 840e 900 84050 8411
  //   2112 20080 84054 8415 2116 40040 4218 8419 20100 a021b 840 8405d 10805e 1210100 4220 600900 21
  //   contents of rom_2 (hex, n*v repeats v):
  //   3 9 6 1c c 17 0 0 f 13 0 0 1a 0 0 21
  //   contents of rom_3 (hex, n*v repeats v):
  //   0 1f
endmodule
